// Logisim project NegCircuit.circ as structural Verilog: 2 circuits, main circuit negative
module negative (
  input  in_1,
  input  in_2,
  input  in_3,
  output Neg
);

  wire and_1_out, and_2_out, and_3_out, and_4_out, not_1_out, not_2_out, not_3_out;

  not not_1 (not_1_out, in_1);
  not not_2 (not_2_out, in_2);
  not not_3 (not_3_out, in_3);
  and and_1 (and_1_out, in_1, not_2_out, not_3_out);
  and and_2 (and_2_out, in_1, not_2_out, in_3);
  and and_3 (and_3_out, in_1, in_2, not_3_out);
  and and_4 (and_4_out, in_1, in_2, in_3);
  or or_1 (Neg, and_1_out, and_2_out, and_3_out, and_4_out);

  // Notes on the sheet:
  //   a2
  //   a1
  //   a0
  //   Neg = a2a1'a0+a2a1'a0+a2a1a0'+a2a1a0
endmodule

module plus_one (
  input  a1,
  input  a0,
  output b1,
  output out_4
);

  wire and_1_out, and_2_out, and_3_out, and_4_out, not_1_out, not_2_out;

  not not_1 (not_1_out, a1);
  not not_2 (not_2_out, a0);
  and and_1 (and_1_out, not_1_out, a0);
  and and_2 (and_2_out, a1, not_2_out);
  and and_3 (and_3_out, not_1_out, a1);
  and and_4 (and_4_out, a1, not_2_out);
  or or_1 (b1, and_1_out, and_2_out);
  or or_2 (out_4, and_3_out, and_4_out);

  // Notes on the sheet:
  //   b1 = a1'a0 + a1a0'
  //   b0 = a1'a0' + a1a0'
endmodule
